# Fritzing sketch simple_neopixel (saved by Fritzing 0.9.3b)

parts:
  Composant1 = Arduino Uno (Rev3)
  LED1 = RGB LED (com. cathode, rgb) [package="5 mm [THT]"]
  R1 = Resistor [tolerance=±5% resistance=470 package=THT]

nets:
  N1: Composant1.D6_PWM, R1.Pin_0
  N2: Composant1.5V, LED1.common_cathode
  N3: Composant1.GND, LED1.green_anode
  N4: LED1.red_anode, R1.Pin_1
